// Logisim project alu.circ as structural Verilog: 8 circuits, main circuit example
module example (
  input  [7:0] in_1,
  input  [7:0] in_2,
  input  [3:0] in_3,
  output [7:0] out_4,
  output out_5,
  output out_6,
  output out_7,
  output out_8,
  output out_9,
  output out_10
);

  ByteALU bytealu_1 (
    .A(in_1), .B(in_2), .Op(in_3), .R(out_4), .Carry(out_5), .AuxiliaryCarry(out_6), .Zero(out_7),
    .Negative(out_8), .EvenParity(out_9), .Overflow(out_10));

  // Notes on the sheet:
  //   0000 AND
  //   0001 NAND
  //   0010 OR
  //   0011 NOR
  //   0100 XOR
  //   0101 XNOR
  //   0110 ADD
  //   0111 SUB
  //   1000 NOT
  //   1001 NEG
  //   1010 INC
  //   1011 DEC
  //   1100 SHR
  //   1101 SHL
  //   1110 SAR
  //   1111 MIRROR
endmodule

module ByteALU (
  input  [7:0] A,
  input  [7:0] B,
  input  [3:0] Op,
  output [7:0] R,
  output Carry,
  output AuxiliaryCarry,
  output Zero,
  output Negative,
  output EvenParity,
  output Overflow
);

  wire ADD_out, and_1_out, and_2_out, and_4_out, decoder_1_out0, decoder_1_out1, decoder_1_out2,
       decoder_1_out3, decoder_1_out4, decoder_1_out5, decoder_1_out6, decoder_1_out7, decoder_1_out8,
       decoder_1_out9, decoder_1_out10, decoder_1_out11, decoder_1_out12, decoder_1_out13, decoder_1_out14,
       decoder_1_out15, multiplexer_4_out, multiplexer_5_out, onebitalu_1_c_out, onebitalu_2_c_out,
       onebitalu_3_c_out, onebitalu_5_c_out, onebitalu_6_c_out, onebitalu_7_c_out, onebitalu_8_c_out,
       or_1_out, or_2_out, or_3_out, or_4_out, or_5_out, or_7_out, sar_1_carry, shl_1_carry, shr_1_carry,
       SUB_out, xor_1_out;
  wire [1:0] priority_encoder_1_out, priority_encoder_2_out, priority_encoder_3_out;
  wire [3:3] or_6_out;
  wire [7:0] multiplexer_1_out, multiplexer_2_out, multiplexer_3_out, onebitalu_1_r, sar_1_r, shl_1_r,
       shr_1_r;

  Decoder #(.enable("false"), .select(4)) decoder_1 (
    .out0(decoder_1_out0), .out1(decoder_1_out1), .out2(decoder_1_out2), .out3(decoder_1_out3),
    .out4(decoder_1_out4), .out5(decoder_1_out5), .out6(decoder_1_out6), .out7(decoder_1_out7),
    .out8(decoder_1_out8), .out9(decoder_1_out9), .out10(decoder_1_out10), .out11(decoder_1_out11),
    .out12(decoder_1_out12), .out13(decoder_1_out13), .out14(decoder_1_out14), .out15(decoder_1_out15),
    .sel(Op));
  or or_1 (or_1_out, decoder_1_out11, decoder_1_out10);
  or or_2 (or_2_out, decoder_1_out0, decoder_1_out1);
  or or_3 (or_3_out, decoder_1_out2, decoder_1_out3);
  or or_4 (or_4_out, decoder_1_out4, decoder_1_out5);
  or or_5 (or_5_out, decoder_1_out1, decoder_1_out3, decoder_1_out5, decoder_1_out8);
  and and_1 (and_1_out, ~or_1_out, ~decoder_1_out9, ~decoder_1_out8);  // AND_Gate
  or SUB (SUB_out, decoder_1_out7, decoder_1_out9, decoder_1_out11);
  Priority_Encoder #(.select(2)) priority_encoder_1 (
    .in0(and_1_out), .in1(or_1_out), .in2(decoder_1_out9), .in3(decoder_1_out8), .out(priority_encoder_1_out));  // open: gs, en_out, en_in
  or ADD (ADD_out, decoder_1_out6, decoder_1_out8, decoder_1_out10, SUB_out);
  Multiplexer #(.select(2), .width(8)) multiplexer_1 (
    .in0(B), .in1(8'h1), .in2(A), .in3({8{1'b0}}), .out(multiplexer_1_out), .sel(priority_encoder_1_out));
  Multiplexer #(.width(8)) multiplexer_2 (
    .in0(A), .in1({8{1'b0}}),
    .out({multiplexer_2_out[0], multiplexer_2_out[1], multiplexer_2_out[2], multiplexer_2_out[3], multiplexer_2_out[4], multiplexer_2_out[5], multiplexer_2_out[6], multiplexer_2_out[7]}),
    .sel(decoder_1_out9));
  Priority_Encoder #(.select(2)) priority_encoder_2 (
    .in0(or_2_out), .in1(or_3_out), .in2(or_4_out), .in3(ADD_out), .out(priority_encoder_2_out));  // open: gs, en_out, en_in
  OneBitALU onebitalu_1 (
    .C_In(SUB_out), .NotOutput(or_5_out), .A(multiplexer_2_out[7]), .NotB(SUB_out), .B(multiplexer_1_out[0]),
    .Op(priority_encoder_2_out), .R(onebitalu_1_r[0]), .C_Out(onebitalu_1_c_out));
  OneBitALU onebitalu_2 (
    .C_In(onebitalu_1_c_out), .NotOutput(or_5_out), .A(multiplexer_2_out[6]), .NotB(SUB_out),
    .B(multiplexer_1_out[1]), .Op(priority_encoder_2_out), .R(onebitalu_1_r[1]), .C_Out(onebitalu_2_c_out));
  OneBitALU onebitalu_3 (
    .C_In(onebitalu_2_c_out), .NotOutput(or_5_out), .A(multiplexer_2_out[5]), .NotB(SUB_out),
    .B(multiplexer_1_out[2]), .Op(priority_encoder_2_out), .R(onebitalu_1_r[2]), .C_Out(onebitalu_3_c_out));
  OneBitALU onebitalu_4 (
    .C_In(onebitalu_3_c_out), .NotOutput(or_5_out), .A(multiplexer_2_out[4]), .NotB(SUB_out),
    .B(multiplexer_1_out[3]), .Op(priority_encoder_2_out), .R(onebitalu_1_r[3]), .C_Out(AuxiliaryCarry));
  OneBitALU onebitalu_5 (
    .C_In(AuxiliaryCarry), .NotOutput(or_5_out), .A(multiplexer_2_out[3]), .NotB(SUB_out),
    .B(multiplexer_1_out[4]), .Op(priority_encoder_2_out), .R(onebitalu_1_r[4]), .C_Out(onebitalu_5_c_out));
  OneBitALU onebitalu_6 (
    .C_In(onebitalu_5_c_out), .NotOutput(or_5_out), .A(multiplexer_2_out[2]), .NotB(SUB_out),
    .B(multiplexer_1_out[5]), .Op(priority_encoder_2_out), .R(onebitalu_1_r[5]), .C_Out(onebitalu_6_c_out));
  OneBitALU onebitalu_7 (
    .C_In(onebitalu_6_c_out), .NotOutput(or_5_out), .A(multiplexer_2_out[1]), .NotB(SUB_out),
    .B(multiplexer_1_out[6]), .Op(priority_encoder_2_out), .R(onebitalu_1_r[6]), .C_Out(onebitalu_7_c_out));
  OneBitALU onebitalu_8 (
    .C_In(onebitalu_7_c_out), .NotOutput(or_5_out), .A(multiplexer_2_out[0]), .NotB(SUB_out),
    .B(multiplexer_1_out[7]), .Op(priority_encoder_2_out), .R(onebitalu_1_r[7]), .C_Out(onebitalu_8_c_out));
  or or_6 (or_6_out[3], B[7], B[6], B[5], B[4], B[3]);
  xor xor_1 (xor_1_out, onebitalu_8_c_out, onebitalu_7_c_out);
  SHR shr_1 (
    .A({multiplexer_2_out[0], multiplexer_2_out[1], multiplexer_2_out[2], multiplexer_2_out[3], multiplexer_2_out[4], multiplexer_2_out[5], multiplexer_2_out[6], multiplexer_2_out[7]}),
    .B({or_6_out[3], B[2:0]}), .R(shr_1_r), .Carry(shr_1_carry));
  SHL shl_1 (
    .A({multiplexer_2_out[0], multiplexer_2_out[1], multiplexer_2_out[2], multiplexer_2_out[3], multiplexer_2_out[4], multiplexer_2_out[5], multiplexer_2_out[6], multiplexer_2_out[7]}),
    .B({or_6_out[3], B[2:0]}), .R(shl_1_r), .Carry(shl_1_carry));
  SAR sar_1 (
    .A({multiplexer_2_out[0], multiplexer_2_out[1], multiplexer_2_out[2], multiplexer_2_out[3], multiplexer_2_out[4], multiplexer_2_out[5], multiplexer_2_out[6], multiplexer_2_out[7]}),
    .B({or_6_out[3], B[2:0]}), .R(sar_1_r), .Carry(sar_1_carry));
  and and_2 (and_2_out, decoder_1_out9, ~Zero);  // AND_Gate
  nor nor_1 (Zero, R[0], R[1], R[2], R[3], R[4], R[5], R[6], Negative);
  NotExactlyOne xnor_1 (
    .out(EvenParity), .in0(R[0]), .in1(R[1]), .in2(R[2]), .in3(R[3]), .in4(R[4]), .in5(R[5]), .in6(R[6]),
    .in7(Negative));
  and and_3 (Overflow, ADD_out, xor_1_out);
  or or_7 (or_7_out, decoder_1_out15, decoder_1_out14, decoder_1_out13, decoder_1_out12);
  Priority_Encoder #(.select(2)) priority_encoder_3 (
    .in0(decoder_1_out12), .in1(decoder_1_out13), .in2(decoder_1_out14), .in3(decoder_1_out15),
    .out(priority_encoder_3_out));  // open: gs, en_out, en_in
  // Probe on priority_encoder_3_out
  Multiplexer #(.select(2), .width(8)) multiplexer_3 (
    .in0(shr_1_r), .in1(shl_1_r), .in2(sar_1_r), .in3(multiplexer_2_out), .out(multiplexer_3_out),
    .sel(priority_encoder_3_out));
  Multiplexer #(.select(2)) multiplexer_4 (
    .in0(shr_1_carry), .in1(shl_1_carry), .in2(sar_1_carry), .out(multiplexer_4_out),
    .sel(priority_encoder_3_out));  // open: in3
  Multiplexer multiplexer_5 (.in0(and_4_out), .in1(and_2_out), .out(multiplexer_5_out), .sel(decoder_1_out9));
  and and_4 (and_4_out, ADD_out, onebitalu_8_c_out);
  Multiplexer #(.width(8)) multiplexer_6 (
    .in0(onebitalu_1_r), .in1(multiplexer_3_out), .out({Negative, R[6:0]}), .sel(or_7_out));
  Multiplexer multiplexer_7 (.in0(multiplexer_5_out), .in1(multiplexer_4_out), .out(Carry), .sel(or_7_out));

  assign R[7] = Negative;

  // Notes on the sheet:
  //   0000 AND
  //   0001 NAND
  //   0010 OR
  //   0011 NOR
  //   0100 XOR
  //   0101 XNOR
  //   0110 ADD
  //   0111 SUB
  //   1000 NOT
  //   1001 NEG
  //   1010 INC
  //   1011 DEC
  //   1100 SHR
  //   1101 SHL
  //   1110 SAR
  //   1111 MIRROR
  //   INC/DEC
  //   AND
  //   NOT
  //   OR
  //   NOT_OUT
  //   XOR
  //   NEG
endmodule

module OneBitALU (
  input  C_In,
  input  NotOutput,
  input  A,
  input  NotB,
  input  B,
  input  [1:0] Op,
  output R,
  output C_Out
);

  wire and_1_out, fulladder_1_fullsum, multiplexer_1_out, or_1_out, xor_1_out, xor_2_out;

  xor xor_1 (xor_1_out, NotB, B);
  and and_1 (and_1_out, A, xor_1_out);
  or or_1 (or_1_out, A, xor_1_out);
  xor xor_2 (xor_2_out, A, xor_1_out);
  FullAdder fulladder_1 (.C(C_In), .X(A), .Y(xor_1_out), .FullSum(fulladder_1_fullsum), .FullCarry(C_Out));
  Multiplexer #(.select(2)) multiplexer_1 (
    .in0(and_1_out), .in1(or_1_out), .in2(xor_2_out), .in3(fulladder_1_fullsum), .out(multiplexer_1_out),
    .sel(Op));
  xor xor_3 (R, NotOutput, multiplexer_1_out);

  // Notes on the sheet:
  //   00 AND
  //   01 OR
  //   10 XOR
  //   11 ADD
endmodule

module SHR (
  input  [7:0] A,
  input  [3:0] B,
  output [7:0] R,
  output Carry
);

  wire multiplexer_1_out, multiplexer_2_out, multiplexer_3_out, multiplexer_4_out, multiplexer_5_out,
       multiplexer_6_out, multiplexer_7_out, multiplexer_8_out, multiplexer_9_out, multiplexer_10_out,
       multiplexer_11_out, multiplexer_12_out, multiplexer_13_out, multiplexer_14_out, multiplexer_15_out,
       multiplexer_16_out, multiplexer_17_out, multiplexer_18_out;
  wire [7:0] multiplexer_20_out;

  Multiplexer multiplexer_1 (.in1(A[0]), .out(multiplexer_1_out), .sel(B[0]));  // open: in0
  Multiplexer multiplexer_2 (.in0(A[0]), .in1(A[1]), .out(multiplexer_2_out), .sel(B[0]));
  Multiplexer multiplexer_3 (.in0(A[1]), .in1(A[2]), .out(multiplexer_3_out), .sel(B[0]));
  Multiplexer multiplexer_4 (.in0(A[2]), .in1(A[3]), .out(multiplexer_4_out), .sel(B[0]));
  Multiplexer multiplexer_5 (.in0(A[3]), .in1(A[4]), .out(multiplexer_5_out), .sel(B[0]));
  Multiplexer multiplexer_6 (.in0(A[4]), .in1(A[5]), .out(multiplexer_6_out), .sel(B[0]));
  Multiplexer multiplexer_7 (.in0(A[5]), .in1(A[6]), .out(multiplexer_7_out), .sel(B[0]));
  Multiplexer multiplexer_8 (.in0(A[6]), .in1(A[7]), .out(multiplexer_8_out), .sel(B[0]));
  Multiplexer multiplexer_9 (.in0(A[7]), .in1(1'b0), .out(multiplexer_9_out), .sel(B[0]));
  Multiplexer multiplexer_10 (.in0(multiplexer_1_out), .in1(multiplexer_3_out), .out(multiplexer_10_out), .sel(B[1]));
  Multiplexer multiplexer_11 (.in0(multiplexer_2_out), .in1(multiplexer_4_out), .out(multiplexer_11_out), .sel(B[1]));
  Multiplexer multiplexer_12 (.in0(multiplexer_3_out), .in1(multiplexer_5_out), .out(multiplexer_12_out), .sel(B[1]));
  Multiplexer multiplexer_13 (.in0(multiplexer_4_out), .in1(multiplexer_6_out), .out(multiplexer_13_out), .sel(B[1]));
  Multiplexer multiplexer_14 (.in0(multiplexer_5_out), .in1(multiplexer_7_out), .out(multiplexer_14_out), .sel(B[1]));
  Multiplexer multiplexer_15 (.in0(multiplexer_6_out), .in1(multiplexer_8_out), .out(multiplexer_15_out), .sel(B[1]));
  Multiplexer multiplexer_16 (.in0(multiplexer_7_out), .in1(multiplexer_9_out), .out(multiplexer_16_out), .sel(B[1]));
  Multiplexer multiplexer_17 (.in0(multiplexer_8_out), .in1(1'b0), .out(multiplexer_17_out), .sel(B[1]));
  Multiplexer multiplexer_18 (.in0(multiplexer_9_out), .in1(1'b0), .out(multiplexer_18_out), .sel(B[1]));
  Multiplexer multiplexer_19 (.in0(multiplexer_10_out), .in1(multiplexer_14_out), .out(Carry), .sel(B[2]));
  Multiplexer multiplexer_20 (
    .in0(multiplexer_11_out), .in1(multiplexer_15_out), .out(multiplexer_20_out[0]), .sel(B[2]));
  Multiplexer multiplexer_21 (
    .in0(multiplexer_12_out), .in1(multiplexer_16_out), .out(multiplexer_20_out[1]), .sel(B[2]));
  Multiplexer multiplexer_22 (
    .in0(multiplexer_13_out), .in1(multiplexer_17_out), .out(multiplexer_20_out[2]), .sel(B[2]));
  Multiplexer multiplexer_23 (
    .in0(multiplexer_14_out), .in1(multiplexer_18_out), .out(multiplexer_20_out[3]), .sel(B[2]));
  Multiplexer multiplexer_24 (.in0(multiplexer_15_out), .in1(1'b0), .out(multiplexer_20_out[4]), .sel(B[2]));
  Multiplexer multiplexer_25 (.in0(multiplexer_16_out), .in1(1'b0), .out(multiplexer_20_out[5]), .sel(B[2]));
  Multiplexer multiplexer_26 (.in0(multiplexer_17_out), .in1(1'b0), .out(multiplexer_20_out[6]), .sel(B[2]));
  Multiplexer multiplexer_27 (.in0(multiplexer_18_out), .in1(1'b0), .out(multiplexer_20_out[7]), .sel(B[2]));
  Multiplexer #(.width(8)) multiplexer_28 (.in0(multiplexer_20_out), .in1({8{1'b0}}), .out(R), .sel(B[3]));
endmodule

module SHL (
  input  [7:0] A,
  input  [3:0] B,
  output [7:0] R,
  output Carry
);

  wire multiplexer_1_out, multiplexer_2_out, multiplexer_3_out, multiplexer_4_out, multiplexer_5_out,
       multiplexer_6_out, multiplexer_7_out, multiplexer_8_out, multiplexer_9_out, multiplexer_10_out,
       multiplexer_11_out, multiplexer_12_out, multiplexer_13_out, multiplexer_14_out, multiplexer_15_out,
       multiplexer_16_out, multiplexer_17_out, multiplexer_18_out;
  wire [7:0] multiplexer_19_out;

  Multiplexer multiplexer_1 (.in0(A[0]), .in1(1'b0), .out(multiplexer_1_out), .sel(B[0]));
  Multiplexer multiplexer_2 (.in0(A[1]), .in1(A[0]), .out(multiplexer_2_out), .sel(B[0]));
  Multiplexer multiplexer_3 (.in0(A[2]), .in1(A[1]), .out(multiplexer_3_out), .sel(B[0]));
  Multiplexer multiplexer_4 (.in0(A[3]), .in1(A[2]), .out(multiplexer_4_out), .sel(B[0]));
  Multiplexer multiplexer_5 (.in0(A[4]), .in1(A[3]), .out(multiplexer_5_out), .sel(B[0]));
  Multiplexer multiplexer_6 (.in0(A[5]), .in1(A[4]), .out(multiplexer_6_out), .sel(B[0]));
  Multiplexer multiplexer_7 (.in0(A[6]), .in1(A[5]), .out(multiplexer_7_out), .sel(B[0]));
  Multiplexer multiplexer_8 (.in0(A[7]), .in1(A[6]), .out(multiplexer_8_out), .sel(B[0]));
  Multiplexer multiplexer_9 (.in1(A[7]), .out(multiplexer_9_out), .sel(B[0]));  // open: in0
  Multiplexer multiplexer_10 (.in0(multiplexer_1_out), .in1(1'b0), .out(multiplexer_10_out), .sel(B[1]));
  Multiplexer multiplexer_11 (.in0(multiplexer_2_out), .in1(1'b0), .out(multiplexer_11_out), .sel(B[1]));
  Multiplexer multiplexer_12 (.in0(multiplexer_3_out), .in1(multiplexer_1_out), .out(multiplexer_12_out), .sel(B[1]));
  Multiplexer multiplexer_13 (.in0(multiplexer_4_out), .in1(multiplexer_2_out), .out(multiplexer_13_out), .sel(B[1]));
  Multiplexer multiplexer_14 (.in0(multiplexer_5_out), .in1(multiplexer_3_out), .out(multiplexer_14_out), .sel(B[1]));
  Multiplexer multiplexer_15 (.in0(multiplexer_6_out), .in1(multiplexer_4_out), .out(multiplexer_15_out), .sel(B[1]));
  Multiplexer multiplexer_16 (.in0(multiplexer_7_out), .in1(multiplexer_5_out), .out(multiplexer_16_out), .sel(B[1]));
  Multiplexer multiplexer_17 (.in0(multiplexer_8_out), .in1(multiplexer_6_out), .out(multiplexer_17_out), .sel(B[1]));
  Multiplexer multiplexer_18 (.in0(multiplexer_9_out), .in1(multiplexer_7_out), .out(multiplexer_18_out), .sel(B[1]));
  Multiplexer multiplexer_19 (.in0(multiplexer_10_out), .in1(1'b0), .out(multiplexer_19_out[0]), .sel(B[2]));
  Multiplexer multiplexer_20 (.in0(multiplexer_11_out), .in1(1'b0), .out(multiplexer_19_out[1]), .sel(B[2]));
  Multiplexer multiplexer_21 (.in0(multiplexer_12_out), .in1(1'b0), .out(multiplexer_19_out[2]), .sel(B[2]));
  Multiplexer multiplexer_22 (.in0(multiplexer_13_out), .in1(1'b0), .out(multiplexer_19_out[3]), .sel(B[2]));
  Multiplexer multiplexer_23 (
    .in0(multiplexer_14_out), .in1(multiplexer_10_out), .out(multiplexer_19_out[4]), .sel(B[2]));
  Multiplexer multiplexer_24 (
    .in0(multiplexer_15_out), .in1(multiplexer_11_out), .out(multiplexer_19_out[5]), .sel(B[2]));
  Multiplexer multiplexer_25 (
    .in0(multiplexer_16_out), .in1(multiplexer_12_out), .out(multiplexer_19_out[6]), .sel(B[2]));
  Multiplexer multiplexer_26 (
    .in0(multiplexer_17_out), .in1(multiplexer_13_out), .out(multiplexer_19_out[7]), .sel(B[2]));
  Multiplexer multiplexer_27 (.in0(multiplexer_18_out), .in1(multiplexer_14_out), .out(Carry), .sel(B[2]));
  Multiplexer #(.width(8)) multiplexer_28 (.in0(multiplexer_19_out), .in1({8{1'b0}}), .out(R), .sel(B[3]));
endmodule

module SAR (
  input  [7:0] A,
  input  [3:0] B,
  output [7:0] R,
  output Carry
);

  wire multiplexer_1_out, multiplexer_2_out, multiplexer_3_out, multiplexer_4_out, multiplexer_5_out,
       multiplexer_6_out, multiplexer_7_out, multiplexer_8_out, multiplexer_9_out, multiplexer_10_out,
       multiplexer_11_out, multiplexer_12_out, multiplexer_13_out, multiplexer_14_out, multiplexer_15_out,
       multiplexer_16_out;
  wire [6:0] multiplexer_18_out;
  wire [7:0] bit_extender_1_out;

  Multiplexer multiplexer_1 (.in1(A[0]), .out(multiplexer_1_out), .sel(B[0]));  // open: in0
  Multiplexer multiplexer_2 (.in0(A[0]), .in1(A[1]), .out(multiplexer_2_out), .sel(B[0]));
  Multiplexer multiplexer_3 (.in0(A[1]), .in1(A[2]), .out(multiplexer_3_out), .sel(B[0]));
  Multiplexer multiplexer_4 (.in0(A[2]), .in1(A[3]), .out(multiplexer_4_out), .sel(B[0]));
  Multiplexer multiplexer_5 (.in0(A[3]), .in1(A[4]), .out(multiplexer_5_out), .sel(B[0]));
  Multiplexer multiplexer_6 (.in0(A[4]), .in1(A[5]), .out(multiplexer_6_out), .sel(B[0]));
  Multiplexer multiplexer_7 (.in0(A[5]), .in1(A[6]), .out(multiplexer_7_out), .sel(B[0]));
  Multiplexer multiplexer_8 (.in0(A[6]), .in1(A[7]), .out(multiplexer_8_out), .sel(B[0]));
  Multiplexer multiplexer_9 (.in0(multiplexer_1_out), .in1(multiplexer_3_out), .out(multiplexer_9_out), .sel(B[1]));
  Multiplexer multiplexer_10 (.in0(multiplexer_2_out), .in1(multiplexer_4_out), .out(multiplexer_10_out), .sel(B[1]));
  Multiplexer multiplexer_11 (.in0(multiplexer_3_out), .in1(multiplexer_5_out), .out(multiplexer_11_out), .sel(B[1]));
  Multiplexer multiplexer_12 (.in0(multiplexer_4_out), .in1(multiplexer_6_out), .out(multiplexer_12_out), .sel(B[1]));
  Multiplexer multiplexer_13 (.in0(multiplexer_5_out), .in1(multiplexer_7_out), .out(multiplexer_13_out), .sel(B[1]));
  Multiplexer multiplexer_14 (.in0(multiplexer_6_out), .in1(multiplexer_8_out), .out(multiplexer_14_out), .sel(B[1]));
  Multiplexer multiplexer_15 (.in0(multiplexer_7_out), .in1(A[7]), .out(multiplexer_15_out), .sel(B[1]));
  Multiplexer multiplexer_16 (.in0(multiplexer_8_out), .in1(A[7]), .out(multiplexer_16_out), .sel(B[1]));
  Multiplexer multiplexer_17 (.in0(multiplexer_9_out), .in1(multiplexer_13_out), .out(Carry), .sel(B[2]));
  Multiplexer multiplexer_18 (
    .in0(multiplexer_10_out), .in1(multiplexer_14_out), .out(multiplexer_18_out[0]), .sel(B[2]));
  Multiplexer multiplexer_19 (
    .in0(multiplexer_11_out), .in1(multiplexer_15_out), .out(multiplexer_18_out[1]), .sel(B[2]));
  Multiplexer multiplexer_20 (
    .in0(multiplexer_12_out), .in1(multiplexer_16_out), .out(multiplexer_18_out[2]), .sel(B[2]));
  Multiplexer multiplexer_21 (.in0(multiplexer_13_out), .in1(A[7]), .out(multiplexer_18_out[3]), .sel(B[2]));
  Multiplexer multiplexer_22 (.in0(multiplexer_14_out), .in1(A[7]), .out(multiplexer_18_out[4]), .sel(B[2]));
  Multiplexer multiplexer_23 (.in0(multiplexer_15_out), .in1(A[7]), .out(multiplexer_18_out[5]), .sel(B[2]));
  Multiplexer multiplexer_24 (.in0(multiplexer_16_out), .in1(A[7]), .out(multiplexer_18_out[6]), .sel(B[2]));
  assign bit_extender_1_out = {{7{A[7]}}, A[7]};  // Bit_Extender bit_extender_1
  Multiplexer #(.width(8)) multiplexer_25 (
    .in0({A[7], multiplexer_18_out}), .in1(bit_extender_1_out), .out(R), .sel(B[3]));
endmodule

module FullAdder (
  input  C,
  input  X,
  input  Y,
  output FullSum,
  output FullCarry
);

  wire halfadder_1_halfcarry, halfadder_1_halfsum, halfadder_2_halfcarry;

  HalfAdder halfadder_1 (.X(X), .Y(Y), .HalfSum(halfadder_1_halfsum), .HalfCarry(halfadder_1_halfcarry));
  HalfAdder halfadder_2 (.X(C), .Y(halfadder_1_halfsum), .HalfSum(FullSum), .HalfCarry(halfadder_2_halfcarry));
  or or_1 (FullCarry, halfadder_2_halfcarry, halfadder_1_halfcarry);
endmodule

module HalfAdder (
  input  X,
  input  Y,
  output HalfSum,
  output HalfCarry
);

  and and_1 (HalfCarry, X, Y);
  xor xor_1 (HalfSum, X, Y);
endmodule
