// Logisim project adders.circ as structural Verilog: 3 circuits, main circuit HalfAdder
module HalfAdder (
  input  X,
  input  Y,
  output HalfSum,
  output HalfCarry
);

  and and_1 (HalfCarry, X, Y);
  xor xor_1 (HalfSum, X, Y);
endmodule

module FullAdder (
  input  C,
  input  X,
  input  Y,
  output FullSum,
  output FullCarry
);

  wire halfadder_1_halfcarry, halfadder_1_halfsum, halfadder_2_halfcarry;

  HalfAdder halfadder_1 (.X(X), .Y(Y), .HalfSum(halfadder_1_halfsum), .HalfCarry(halfadder_1_halfcarry));
  HalfAdder halfadder_2 (.X(C), .Y(halfadder_1_halfsum), .HalfSum(FullSum), .HalfCarry(halfadder_2_halfcarry));
  or or_1 (FullCarry, halfadder_2_halfcarry, halfadder_1_halfcarry);
endmodule

module ByteAdderSubtractor (
  input  A0,
  input  A1,
  input  A2,
  input  A3,
  input  A4,
  input  A5,
  input  A6,
  input  A7,
  input  B0,
  input  B1,
  input  B2,
  input  B3,
  input  B4,
  input  B5,
  input  B6,
  input  B7,
  input  EnableSub,
  output R0,
  output R1,
  output R2,
  output R3,
  output R4,
  output R5,
  output R6,
  output R7,
  output Carry
);

  wire fulladder_1_fullcarry, fulladder_2_fullcarry, fulladder_3_fullcarry, fulladder_4_fullcarry,
       fulladder_5_fullcarry, fulladder_6_fullcarry, fulladder_7_fullcarry, xor_1_out, xor_2_out, xor_3_out,
       xor_4_out, xor_5_out, xor_6_out, xor_7_out, xor_8_out;

  xor xor_1 (xor_1_out, EnableSub, B0);
  xor xor_2 (xor_2_out, EnableSub, B1);
  xor xor_3 (xor_3_out, EnableSub, B2);
  xor xor_4 (xor_4_out, EnableSub, B3);
  xor xor_5 (xor_5_out, EnableSub, B4);
  xor xor_6 (xor_6_out, EnableSub, B5);
  xor xor_7 (xor_7_out, EnableSub, B6);
  xor xor_8 (xor_8_out, EnableSub, B7);
  FullAdder fulladder_1 (.C(EnableSub), .X(A0), .Y(xor_1_out), .FullSum(R0), .FullCarry(fulladder_1_fullcarry));
  FullAdder fulladder_2 (
    .C(fulladder_1_fullcarry), .X(A1), .Y(xor_2_out), .FullSum(R1), .FullCarry(fulladder_2_fullcarry));
  FullAdder fulladder_3 (
    .C(fulladder_2_fullcarry), .X(A2), .Y(xor_3_out), .FullSum(R2), .FullCarry(fulladder_3_fullcarry));
  FullAdder fulladder_4 (
    .C(fulladder_3_fullcarry), .X(A3), .Y(xor_4_out), .FullSum(R3), .FullCarry(fulladder_4_fullcarry));
  FullAdder fulladder_5 (
    .C(fulladder_4_fullcarry), .X(A4), .Y(xor_5_out), .FullSum(R4), .FullCarry(fulladder_5_fullcarry));
  FullAdder fulladder_6 (
    .C(fulladder_5_fullcarry), .X(A5), .Y(xor_6_out), .FullSum(R5), .FullCarry(fulladder_6_fullcarry));
  FullAdder fulladder_7 (
    .C(fulladder_6_fullcarry), .X(A6), .Y(xor_7_out), .FullSum(R6), .FullCarry(fulladder_7_fullcarry));
  FullAdder fulladder_8 (.C(fulladder_7_fullcarry), .X(A7), .Y(xor_8_out), .FullSum(R7), .FullCarry(Carry));
endmodule
