// Logisim project multipliers.circ as structural Verilog: 3 circuits, main circuit main
module main (
  input  [7:0] in_1,
  input  [7:0] in_2,
  output [7:0] out_3,
  output [7:0] out_4
);

  ByteMultiplier bytemultiplier_1 (
    .A0(in_1[0]), .A1(in_1[1]), .A2(in_1[2]), .A3(in_1[3]), .A4(in_1[4]), .A5(in_1[5]), .A6(in_1[6]),
    .A7(in_1[7]), .B0(in_2[0]), .B1(in_2[1]), .B2(in_2[2]), .B3(in_2[3]), .B4(in_2[4]), .B5(in_2[5]),
    .B6(in_2[6]), .B7(in_2[7]), .R0(out_3[0]), .R1(out_3[1]), .R2(out_3[2]), .R3(out_3[3]), .R4(out_3[4]),
    .R5(out_3[5]), .R6(out_3[6]), .R7(out_3[7]), .R8(out_4[0]), .R9(out_4[1]), .R10(out_4[2]),
    .R11(out_4[3]), .R12(out_4[4]), .R13(out_4[5]), .R14(out_4[6]), .R15(out_4[7]));
endmodule

module ByteMultiplier (
  input  A0,
  input  A1,
  input  A2,
  input  A3,
  input  A4,
  input  A5,
  input  A6,
  input  A7,
  input  B0,
  input  B1,
  input  B2,
  input  B3,
  input  B4,
  input  B5,
  input  B6,
  input  B7,
  output R0,
  output R1,
  output R2,
  output R3,
  output R4,
  output R5,
  output R6,
  output R7,
  output R8,
  output R9,
  output R10,
  output R11,
  output R12,
  output R13,
  output R14,
  output R15
);

  wire bitbytemultiplier_1_r1, bitbytemultiplier_1_r2, bitbytemultiplier_1_r3, bitbytemultiplier_1_r4,
       bitbytemultiplier_1_r5, bitbytemultiplier_1_r6, bitbytemultiplier_1_r7, bitbytemultiplier_2_r0,
       bitbytemultiplier_2_r1, bitbytemultiplier_2_r2, bitbytemultiplier_2_r3, bitbytemultiplier_2_r4,
       bitbytemultiplier_2_r5, bitbytemultiplier_2_r6, bitbytemultiplier_2_r7, bitbytemultiplier_3_r0,
       bitbytemultiplier_3_r1, bitbytemultiplier_3_r2, bitbytemultiplier_3_r3, bitbytemultiplier_3_r4,
       bitbytemultiplier_3_r5, bitbytemultiplier_3_r6, bitbytemultiplier_3_r7, bitbytemultiplier_4_r0,
       bitbytemultiplier_4_r1, bitbytemultiplier_4_r2, bitbytemultiplier_4_r3, bitbytemultiplier_4_r4,
       bitbytemultiplier_4_r5, bitbytemultiplier_4_r6, bitbytemultiplier_4_r7, bitbytemultiplier_5_r0,
       bitbytemultiplier_5_r1, bitbytemultiplier_5_r2, bitbytemultiplier_5_r3, bitbytemultiplier_5_r4,
       bitbytemultiplier_5_r5, bitbytemultiplier_5_r6, bitbytemultiplier_5_r7, bitbytemultiplier_6_r0,
       bitbytemultiplier_6_r1, bitbytemultiplier_6_r2, bitbytemultiplier_6_r3, bitbytemultiplier_6_r4,
       bitbytemultiplier_6_r5, bitbytemultiplier_6_r6, bitbytemultiplier_6_r7, bitbytemultiplier_7_r0,
       bitbytemultiplier_7_r1, bitbytemultiplier_7_r2, bitbytemultiplier_7_r3, bitbytemultiplier_7_r4,
       bitbytemultiplier_7_r5, bitbytemultiplier_7_r6, bitbytemultiplier_7_r7, bitbytemultiplier_8_r0,
       bitbytemultiplier_8_r1, bitbytemultiplier_8_r2, bitbytemultiplier_8_r3, bitbytemultiplier_8_r4,
       bitbytemultiplier_8_r5, bitbytemultiplier_8_r6, bitbytemultiplier_8_r7, fulladder_1_fullcarry,
       fulladder_1_fullsum, fulladder_2_fullcarry, fulladder_2_fullsum, fulladder_3_fullcarry,
       fulladder_3_fullsum, fulladder_4_fullcarry, fulladder_4_fullsum, fulladder_5_fullcarry,
       fulladder_5_fullsum, fulladder_6_fullcarry, fulladder_6_fullsum, fulladder_7_fullcarry,
       fulladder_7_fullsum, fulladder_8_fullcarry, fulladder_8_fullsum, fulladder_9_fullcarry,
       fulladder_9_fullsum, fulladder_10_fullcarry, fulladder_10_fullsum, fulladder_11_fullcarry,
       fulladder_11_fullsum, fulladder_12_fullcarry, fulladder_12_fullsum, fulladder_13_fullcarry,
       fulladder_13_fullsum, fulladder_14_fullcarry, fulladder_14_fullsum, fulladder_15_fullcarry,
       fulladder_15_fullsum, fulladder_16_fullcarry, fulladder_16_fullsum, fulladder_17_fullcarry,
       fulladder_17_fullsum, fulladder_18_fullcarry, fulladder_18_fullsum, fulladder_19_fullcarry,
       fulladder_19_fullsum, fulladder_20_fullcarry, fulladder_20_fullsum, fulladder_21_fullcarry,
       fulladder_21_fullsum, fulladder_22_fullcarry, fulladder_22_fullsum, fulladder_23_fullcarry,
       fulladder_23_fullsum, fulladder_24_fullcarry, fulladder_24_fullsum, fulladder_25_fullcarry,
       fulladder_25_fullsum, fulladder_26_fullcarry, fulladder_26_fullsum, fulladder_27_fullcarry,
       fulladder_27_fullsum, fulladder_28_fullcarry, fulladder_28_fullsum, fulladder_29_fullcarry,
       fulladder_29_fullsum, fulladder_30_fullcarry, fulladder_30_fullsum, fulladder_31_fullcarry,
       fulladder_31_fullsum, fulladder_32_fullcarry, fulladder_32_fullsum, fulladder_33_fullcarry,
       fulladder_33_fullsum, fulladder_34_fullcarry, fulladder_34_fullsum, fulladder_35_fullcarry,
       fulladder_35_fullsum, fulladder_36_fullcarry, fulladder_37_fullcarry, fulladder_38_fullcarry,
       fulladder_39_fullcarry, fulladder_40_fullcarry, fulladder_41_fullcarry, fulladder_42_fullcarry,
       fulladder_43_fullcarry, fulladder_44_fullcarry, fulladder_45_fullcarry, fulladder_46_fullcarry,
       fulladder_47_fullcarry, halfadder_1_halfcarry, halfadder_1_halfsum, halfadder_2_halfcarry,
       halfadder_2_halfsum, halfadder_3_halfcarry, halfadder_3_halfsum, halfadder_4_halfcarry,
       halfadder_4_halfsum, halfadder_5_halfcarry, halfadder_5_halfsum, halfadder_6_halfcarry,
       halfadder_6_halfsum, halfadder_7_halfcarry, halfadder_7_halfsum, halfadder_8_halfcarry;

  BitByteMultiplier bitbytemultiplier_1 (
    .A7(A7), .A6(A6), .A5(A5), .A4(A4), .A3(A3), .A2(A2), .A1(A1), .A0(A0), .B(B0),
    .R7(bitbytemultiplier_1_r7), .R6(bitbytemultiplier_1_r6), .R5(bitbytemultiplier_1_r5),
    .R4(bitbytemultiplier_1_r4), .R3(bitbytemultiplier_1_r3), .R2(bitbytemultiplier_1_r2),
    .R1(bitbytemultiplier_1_r1), .R0(R0));
  BitByteMultiplier bitbytemultiplier_2 (
    .A7(A7), .A6(A6), .A5(A5), .A4(A4), .A3(A3), .A2(A2), .A1(A1), .A0(A0), .B(B1),
    .R7(bitbytemultiplier_2_r7), .R6(bitbytemultiplier_2_r6), .R5(bitbytemultiplier_2_r5),
    .R4(bitbytemultiplier_2_r4), .R3(bitbytemultiplier_2_r3), .R2(bitbytemultiplier_2_r2),
    .R1(bitbytemultiplier_2_r1), .R0(bitbytemultiplier_2_r0));
  BitByteMultiplier bitbytemultiplier_3 (
    .A7(A7), .A6(A6), .A5(A5), .A4(A4), .A3(A3), .A2(A2), .A1(A1), .A0(A0), .B(B2),
    .R7(bitbytemultiplier_3_r7), .R6(bitbytemultiplier_3_r6), .R5(bitbytemultiplier_3_r5),
    .R4(bitbytemultiplier_3_r4), .R3(bitbytemultiplier_3_r3), .R2(bitbytemultiplier_3_r2),
    .R1(bitbytemultiplier_3_r1), .R0(bitbytemultiplier_3_r0));
  BitByteMultiplier bitbytemultiplier_4 (
    .A7(A7), .A6(A6), .A5(A5), .A4(A4), .A3(A3), .A2(A2), .A1(A1), .A0(A0), .B(B3),
    .R7(bitbytemultiplier_4_r7), .R6(bitbytemultiplier_4_r6), .R5(bitbytemultiplier_4_r5),
    .R4(bitbytemultiplier_4_r4), .R3(bitbytemultiplier_4_r3), .R2(bitbytemultiplier_4_r2),
    .R1(bitbytemultiplier_4_r1), .R0(bitbytemultiplier_4_r0));
  BitByteMultiplier bitbytemultiplier_5 (
    .A7(A7), .A6(A6), .A5(A5), .A4(A4), .A3(A3), .A2(A2), .A1(A1), .A0(A0), .B(B4),
    .R7(bitbytemultiplier_5_r7), .R6(bitbytemultiplier_5_r6), .R5(bitbytemultiplier_5_r5),
    .R4(bitbytemultiplier_5_r4), .R3(bitbytemultiplier_5_r3), .R2(bitbytemultiplier_5_r2),
    .R1(bitbytemultiplier_5_r1), .R0(bitbytemultiplier_5_r0));
  BitByteMultiplier bitbytemultiplier_6 (
    .A7(A7), .A6(A6), .A5(A5), .A4(A4), .A3(A3), .A2(A2), .A1(A1), .A0(A0), .B(B5),
    .R7(bitbytemultiplier_6_r7), .R6(bitbytemultiplier_6_r6), .R5(bitbytemultiplier_6_r5),
    .R4(bitbytemultiplier_6_r4), .R3(bitbytemultiplier_6_r3), .R2(bitbytemultiplier_6_r2),
    .R1(bitbytemultiplier_6_r1), .R0(bitbytemultiplier_6_r0));
  BitByteMultiplier bitbytemultiplier_7 (
    .A7(A7), .A6(A6), .A5(A5), .A4(A4), .A3(A3), .A2(A2), .A1(A1), .A0(A0), .B(B6),
    .R7(bitbytemultiplier_7_r7), .R6(bitbytemultiplier_7_r6), .R5(bitbytemultiplier_7_r5),
    .R4(bitbytemultiplier_7_r4), .R3(bitbytemultiplier_7_r3), .R2(bitbytemultiplier_7_r2),
    .R1(bitbytemultiplier_7_r1), .R0(bitbytemultiplier_7_r0));
  BitByteMultiplier bitbytemultiplier_8 (
    .A7(A7), .A6(A6), .A5(A5), .A4(A4), .A3(A3), .A2(A2), .A1(A1), .A0(A0), .B(B7),
    .R7(bitbytemultiplier_8_r7), .R6(bitbytemultiplier_8_r6), .R5(bitbytemultiplier_8_r5),
    .R4(bitbytemultiplier_8_r4), .R3(bitbytemultiplier_8_r3), .R2(bitbytemultiplier_8_r2),
    .R1(bitbytemultiplier_8_r1), .R0(bitbytemultiplier_8_r0));
  HalfAdder halfadder_1 (
    .X(bitbytemultiplier_1_r6), .Y(bitbytemultiplier_2_r5), .HalfSum(halfadder_1_halfsum),
    .HalfCarry(halfadder_1_halfcarry));
  FullAdder fulladder_1 (
    .C(bitbytemultiplier_1_r7), .X(bitbytemultiplier_2_r6), .Y(bitbytemultiplier_3_r5),
    .FullSum(fulladder_1_fullsum), .FullCarry(fulladder_1_fullcarry));
  FullAdder fulladder_2 (
    .C(bitbytemultiplier_2_r7), .X(bitbytemultiplier_3_r6), .Y(bitbytemultiplier_4_r5),
    .FullSum(fulladder_2_fullsum), .FullCarry(fulladder_2_fullcarry));
  FullAdder fulladder_3 (
    .C(bitbytemultiplier_3_r7), .X(bitbytemultiplier_4_r6), .Y(bitbytemultiplier_5_r5),
    .FullSum(fulladder_3_fullsum), .FullCarry(fulladder_3_fullcarry));
  HalfAdder halfadder_2 (
    .X(bitbytemultiplier_4_r4), .Y(bitbytemultiplier_5_r3), .HalfSum(halfadder_2_halfsum),
    .HalfCarry(halfadder_2_halfcarry));
  HalfAdder halfadder_3 (
    .X(bitbytemultiplier_5_r4), .Y(bitbytemultiplier_6_r3), .HalfSum(halfadder_3_halfsum),
    .HalfCarry(halfadder_3_halfcarry));
  HalfAdder halfadder_4 (
    .X(bitbytemultiplier_1_r4), .Y(bitbytemultiplier_2_r3), .HalfSum(halfadder_4_halfsum),
    .HalfCarry(halfadder_4_halfcarry));
  FullAdder fulladder_4 (
    .C(bitbytemultiplier_1_r5), .X(bitbytemultiplier_3_r3), .Y(bitbytemultiplier_4_r2),
    .FullSum(fulladder_4_fullsum), .FullCarry(fulladder_4_fullcarry));
  FullAdder fulladder_5 (
    .C(halfadder_1_halfsum), .X(bitbytemultiplier_3_r4), .Y(bitbytemultiplier_4_r3),
    .FullSum(fulladder_5_fullsum), .FullCarry(fulladder_5_fullcarry));
  FullAdder fulladder_6 (
    .C(halfadder_1_halfcarry), .X(fulladder_1_fullsum), .Y(halfadder_2_halfsum),
    .FullSum(fulladder_6_fullsum), .FullCarry(fulladder_6_fullcarry));
  FullAdder fulladder_7 (
    .C(fulladder_1_fullcarry), .X(halfadder_2_halfcarry), .Y(fulladder_2_fullsum),
    .FullSum(fulladder_7_fullsum), .FullCarry(fulladder_7_fullcarry));
  FullAdder fulladder_8 (
    .C(fulladder_2_fullcarry), .X(halfadder_3_halfcarry), .Y(fulladder_3_fullsum),
    .FullSum(fulladder_8_fullsum), .FullCarry(fulladder_8_fullcarry));
  FullAdder fulladder_9 (
    .C(fulladder_3_fullcarry), .X(bitbytemultiplier_5_r6), .Y(bitbytemultiplier_4_r7),
    .FullSum(fulladder_9_fullsum), .FullCarry(fulladder_9_fullcarry));
  FullAdder fulladder_10 (
    .C(bitbytemultiplier_6_r6), .X(bitbytemultiplier_5_r7), .Y(bitbytemultiplier_7_r5),
    .FullSum(fulladder_10_fullsum), .FullCarry(fulladder_10_fullcarry));
  HalfAdder halfadder_5 (
    .X(bitbytemultiplier_2_r4), .Y(bitbytemultiplier_5_r1), .HalfSum(halfadder_5_halfsum),
    .HalfCarry(halfadder_5_halfcarry));
  FullAdder fulladder_11 (
    .C(bitbytemultiplier_5_r2), .X(bitbytemultiplier_6_r1), .Y(bitbytemultiplier_7_r0),
    .FullSum(fulladder_11_fullsum), .FullCarry(fulladder_11_fullcarry));
  FullAdder fulladder_12 (
    .C(bitbytemultiplier_6_r2), .X(bitbytemultiplier_7_r1), .Y(bitbytemultiplier_8_r0),
    .FullSum(fulladder_12_fullsum), .FullCarry(fulladder_12_fullcarry));
  FullAdder fulladder_13 (
    .C(bitbytemultiplier_8_r1), .X(halfadder_3_halfsum), .Y(bitbytemultiplier_7_r2),
    .FullSum(fulladder_13_fullsum), .FullCarry(fulladder_13_fullcarry));
  FullAdder fulladder_14 (
    .C(bitbytemultiplier_8_r2), .X(bitbytemultiplier_7_r3), .Y(bitbytemultiplier_6_r4),
    .FullSum(fulladder_14_fullsum), .FullCarry(fulladder_14_fullcarry));
  FullAdder fulladder_15 (
    .C(bitbytemultiplier_8_r3), .X(bitbytemultiplier_7_r4), .Y(bitbytemultiplier_6_r5),
    .FullSum(fulladder_15_fullsum), .FullCarry(fulladder_15_fullcarry));
  HalfAdder halfadder_6 (
    .X(bitbytemultiplier_1_r3), .Y(bitbytemultiplier_2_r2), .HalfSum(halfadder_6_halfsum),
    .HalfCarry(halfadder_6_halfcarry));
  FullAdder fulladder_16 (
    .C(halfadder_4_halfsum), .X(bitbytemultiplier_3_r2), .Y(bitbytemultiplier_4_r1),
    .FullSum(fulladder_16_fullsum), .FullCarry(fulladder_16_fullcarry));
  FullAdder fulladder_17 (
    .C(fulladder_4_fullsum), .X(halfadder_4_halfcarry), .Y(halfadder_5_halfsum),
    .FullSum(fulladder_17_fullsum), .FullCarry(fulladder_17_fullcarry));
  FullAdder fulladder_18 (
    .C(fulladder_5_fullsum), .X(fulladder_4_fullcarry), .Y(halfadder_5_halfcarry),
    .FullSum(fulladder_18_fullsum), .FullCarry(fulladder_18_fullcarry));
  FullAdder fulladder_19 (
    .C(fulladder_5_fullcarry), .X(fulladder_11_fullcarry), .Y(fulladder_6_fullsum),
    .FullSum(fulladder_19_fullsum), .FullCarry(fulladder_19_fullcarry));
  FullAdder fulladder_20 (
    .C(fulladder_6_fullcarry), .X(fulladder_12_fullcarry), .Y(fulladder_7_fullsum),
    .FullSum(fulladder_20_fullsum), .FullCarry(fulladder_20_fullcarry));
  FullAdder fulladder_21 (
    .C(fulladder_7_fullcarry), .X(fulladder_13_fullcarry), .Y(fulladder_8_fullsum),
    .FullSum(fulladder_21_fullsum), .FullCarry(fulladder_21_fullcarry));
  FullAdder fulladder_22 (
    .C(fulladder_9_fullsum), .X(fulladder_8_fullcarry), .Y(fulladder_14_fullcarry),
    .FullSum(fulladder_22_fullsum), .FullCarry(fulladder_22_fullcarry));
  FullAdder fulladder_23 (
    .C(fulladder_9_fullcarry), .X(fulladder_15_fullcarry), .Y(bitbytemultiplier_8_r4),
    .FullSum(fulladder_23_fullsum), .FullCarry(fulladder_23_fullcarry));
  FullAdder fulladder_24 (
    .C(bitbytemultiplier_6_r7), .X(bitbytemultiplier_7_r6), .Y(fulladder_10_fullcarry),
    .FullSum(fulladder_24_fullsum), .FullCarry(fulladder_24_fullcarry));
  HalfAdder halfadder_7 (
    .X(bitbytemultiplier_1_r2), .Y(bitbytemultiplier_2_r1), .HalfSum(halfadder_7_halfsum),
    .HalfCarry(halfadder_7_halfcarry));
  FullAdder fulladder_25 (
    .C(halfadder_6_halfsum), .X(bitbytemultiplier_3_r1), .Y(bitbytemultiplier_4_r0),
    .FullSum(fulladder_25_fullsum), .FullCarry(fulladder_25_fullcarry));
  FullAdder fulladder_26 (
    .C(halfadder_6_halfcarry), .X(fulladder_16_fullsum), .Y(bitbytemultiplier_5_r0),
    .FullSum(fulladder_26_fullsum), .FullCarry(fulladder_26_fullcarry));
  FullAdder fulladder_27 (
    .C(bitbytemultiplier_6_r0), .X(fulladder_16_fullcarry), .Y(fulladder_17_fullsum),
    .FullSum(fulladder_27_fullsum), .FullCarry(fulladder_27_fullcarry));
  FullAdder fulladder_28 (
    .C(fulladder_11_fullsum), .X(fulladder_17_fullcarry), .Y(fulladder_18_fullsum),
    .FullSum(fulladder_28_fullsum), .FullCarry(fulladder_28_fullcarry));
  FullAdder fulladder_29 (
    .C(fulladder_12_fullsum), .X(fulladder_18_fullcarry), .Y(fulladder_19_fullsum),
    .FullSum(fulladder_29_fullsum), .FullCarry(fulladder_29_fullcarry));
  FullAdder fulladder_30 (
    .C(fulladder_19_fullcarry), .X(fulladder_20_fullsum), .Y(fulladder_13_fullsum),
    .FullSum(fulladder_30_fullsum), .FullCarry(fulladder_30_fullcarry));
  FullAdder fulladder_31 (
    .C(fulladder_20_fullcarry), .X(fulladder_14_fullsum), .Y(fulladder_21_fullsum),
    .FullSum(fulladder_31_fullsum), .FullCarry(fulladder_31_fullcarry));
  FullAdder fulladder_32 (
    .C(fulladder_21_fullcarry), .X(fulladder_15_fullsum), .Y(fulladder_22_fullsum),
    .FullSum(fulladder_32_fullsum), .FullCarry(fulladder_32_fullcarry));
  FullAdder fulladder_33 (
    .C(fulladder_22_fullcarry), .X(fulladder_23_fullsum), .Y(fulladder_10_fullsum),
    .FullSum(fulladder_33_fullsum), .FullCarry(fulladder_33_fullcarry));
  FullAdder fulladder_34 (
    .C(fulladder_23_fullcarry), .X(fulladder_24_fullsum), .Y(bitbytemultiplier_8_r5),
    .FullSum(fulladder_34_fullsum), .FullCarry(fulladder_34_fullcarry));
  FullAdder fulladder_35 (
    .C(bitbytemultiplier_7_r7), .X(bitbytemultiplier_8_r6), .Y(fulladder_24_fullcarry),
    .FullSum(fulladder_35_fullsum), .FullCarry(fulladder_35_fullcarry));
  HalfAdder halfadder_8 (
    .X(bitbytemultiplier_1_r1), .Y(bitbytemultiplier_2_r0), .HalfSum(R1), .HalfCarry(halfadder_8_halfcarry));
  FullAdder fulladder_36 (
    .C(halfadder_8_halfcarry), .X(bitbytemultiplier_3_r0), .Y(halfadder_7_halfsum), .FullSum(R2),
    .FullCarry(fulladder_36_fullcarry));
  FullAdder fulladder_37 (
    .C(fulladder_36_fullcarry), .X(halfadder_7_halfcarry), .Y(fulladder_25_fullsum), .FullSum(R3),
    .FullCarry(fulladder_37_fullcarry));
  FullAdder fulladder_38 (
    .C(fulladder_37_fullcarry), .X(fulladder_25_fullcarry), .Y(fulladder_26_fullsum), .FullSum(R4),
    .FullCarry(fulladder_38_fullcarry));
  FullAdder fulladder_39 (
    .C(fulladder_38_fullcarry), .X(fulladder_26_fullcarry), .Y(fulladder_27_fullsum), .FullSum(R5),
    .FullCarry(fulladder_39_fullcarry));
  FullAdder fulladder_40 (
    .C(fulladder_39_fullcarry), .X(fulladder_27_fullcarry), .Y(fulladder_28_fullsum), .FullSum(R6),
    .FullCarry(fulladder_40_fullcarry));
  FullAdder fulladder_41 (
    .C(fulladder_40_fullcarry), .X(fulladder_28_fullcarry), .Y(fulladder_29_fullsum), .FullSum(R7),
    .FullCarry(fulladder_41_fullcarry));
  FullAdder fulladder_42 (
    .C(fulladder_41_fullcarry), .X(fulladder_29_fullcarry), .Y(fulladder_30_fullsum), .FullSum(R8),
    .FullCarry(fulladder_42_fullcarry));
  FullAdder fulladder_43 (
    .C(fulladder_42_fullcarry), .X(fulladder_30_fullcarry), .Y(fulladder_31_fullsum), .FullSum(R9),
    .FullCarry(fulladder_43_fullcarry));
  FullAdder fulladder_44 (
    .C(fulladder_43_fullcarry), .X(fulladder_31_fullcarry), .Y(fulladder_32_fullsum), .FullSum(R10),
    .FullCarry(fulladder_44_fullcarry));
  FullAdder fulladder_45 (
    .C(fulladder_44_fullcarry), .X(fulladder_32_fullcarry), .Y(fulladder_33_fullsum), .FullSum(R11),
    .FullCarry(fulladder_45_fullcarry));
  FullAdder fulladder_46 (
    .C(fulladder_45_fullcarry), .X(fulladder_33_fullcarry), .Y(fulladder_34_fullsum), .FullSum(R12),
    .FullCarry(fulladder_46_fullcarry));
  FullAdder fulladder_47 (
    .C(fulladder_46_fullcarry), .X(fulladder_34_fullcarry), .Y(fulladder_35_fullsum), .FullSum(R13),
    .FullCarry(fulladder_47_fullcarry));
  FullAdder fulladder_48 (
    .C(fulladder_47_fullcarry), .X(bitbytemultiplier_8_r7), .Y(fulladder_35_fullcarry), .FullSum(R14),
    .FullCarry(R15));

  // Notes on the sheet:
  //   w1
  //   w2
  //   w4
  //   w8
  //   w16
  //   w32
  //   w64
  //   w128
  //   w2
  //   w4
  //   w8
  //   w16
  //   w32
  //   w64
  //   w128
  //   w256
  //   w4
  //   w8
  //   w16
  //   w32
  //   w64
  //   w128
  //   w256
  //   w512
  //   w8
  //   w16
  //   w32
  //   w64
  //   w128
  //   w256
  //   w512
  //   w1024
  //   w16
  //   w32
  //   w64
  //   w128
  //   w256
  //   w512
  //   w1024
  //   w2048
  //   w32
  //   w64
  //   w128
  //   w256
  //   w512
  //   w1024
  //   w2048
  //   w4096
  //   w64
  //   w128
  //   w256
  //   w512
  //   w1024
  //   w2048
  //   w4096
  //   w8192
  //   w128
  //   w256
  //   w512
  //   w1024
  //   w2048
  //   w4096
  //   w8192
  //   w16384
  //   Stage1
  //   w64
  //   w128
  //   w128
  //   w256
  //   w256
  //   w512
  //   w512
  //   w1024
  //   w128
  //   w256
  //   w256
  //   w512
  //   w1
  //   w2
  //   w4
  //   w8
  //   w16
  //   w32
  //   w64
  //   w128
  //   w2
  //   w4
  //   w8
  //   w16
  //   w32
  //   w64
  //   w128
  //   w256
  //   w4
  //   w8
  //   w16
  //   w32
  //   w64
  //   w128
  //   w256
  //   w512
  //   w8
  //   w16
  //   w32
  //   w64
  //   w128
  //   w256
  //   w512
  //   w1024
  //   w16
  //   w32
  //   w64
  //   w128
  //   w256
  //   w512
  //   w1024
  //   w2048
  //   w32
  //   w64
  //   w128
  //   w256
  //   w512
  //   w1024
  //   w2048
  //   w4096
  //   w256
  //   w512
  //   w1024
  //   w2048
  //   w4096
  //   w8192
  //   w512
  //   w1024
  //   w2048
  //   w4096
  //   w8192
  //   w16384
  //   w1024
  //   Stage2
  //   w16
  //   w32
  //   w32
  //   w64
  //   w32
  //   w64
  //   w64
  //   w128
  //   w64
  //   w128
  //   w128
  //   w256
  //   w128
  //   w256
  //   w256
  //   w512
  //   w256
  //   w512
  //   w512
  //   w1024
  //   w512
  //   w1024
  //   w1024
  //   w2048
  //   w1024
  //   w2048
  //   w2048
  //   w4096
  //   w1
  //   w2
  //   w4
  //   w8
  //   w16
  //   w32
  //   w64
  //   w128
  //   w2
  //   w4
  //   w8
  //   w16
  //   w32
  //   w64
  //   w128
  //   w256
  //   w4
  //   w8
  //   w16
  //   w32
  //   w64
  //   w128
  //   w256
  //   w512
  //   w8
  //   w16
  //   w32
  //   w64
  //   w128
  //   w256
  //   w512
  //   w1024
  //   w256
  //   w512
  //   w1024
  //   w2048
  //   w512
  //   w1024
  //   w2048
  //   w4096
  //   w1024
  //   w2048
  //   w4096
  //   w8192
  //   w2048
  //   w4096
  //   w8192
  //   w16384
  //   w4096
  //   Stage3
  //   w32
  //   w64
  //   w8
  //   w16
  //   w16
  //   w32
  //   w64
  //   w128
  //   w128
  //   w256
  //   w256
  //   w512
  //   w512
  //   w1024
  //   w1024
  //   w2048
  //   w2048
  //   w4096
  //   w4096
  //   w8192
  //   w1
  //   w2
  //   w4
  //   w8
  //   w16
  //   w32
  //   w64
  //   w128
  //   w2
  //   w4
  //   w8
  //   w16
  //   w32
  //   w64
  //   w128
  //   w256
  //   w4
  //   w8
  //   w16
  //   w32
  //   w64
  //   w128
  //   w256
  //   w512
  //   w256
  //   w512
  //   w1024
  //   w512
  //   w1024
  //   w2048
  //   w1024
  //   w2048
  //   w4096
  //   w2048
  //   w4096
  //   w8192
  //   w4096
  //   w8192
  //   w16384
  //   w8192
  //   Stage4
  //   w1
  //   w2
  //   w2
  //   w4
  //   w4
  //   w8
  //   w8
  //   w16
  //   w16
  //   w32
  //   w32
  //   w64
  //   w64
  //   w128
  //   w128
  //   w256
  //   w256
  //   w512
  //   w512
  //   w1024
  //   w1024
  //   w2048
  //   w2048
  //   w4096
  //   w4096
  //   w8192
  //   w8192
  //   w16384
  //   w16384
  //   FinalAdd
  //   w4
  //   w1
  //   w2
  //   w4
  //   w8
  //   w8
  //   w16
  //   w16
  //   w32
  //   w32
  //   w64
  //   w64
  //   w128
  //   w128
  //   w256
  //   w256
  //   w512
  //   w512
  //   w1024
  //   w1024
  //   w2048
  //   w2048
  //   w4096
  //   w4096
  //   w8192
  //   w8192
  //   w16384
  //   w16384
  //   w32768
endmodule

module BitByteMultiplier (
  input  A7,
  input  A6,
  input  A5,
  input  A4,
  input  A3,
  input  A2,
  input  A1,
  input  A0,
  input  B,
  output R7,
  output R6,
  output R5,
  output R4,
  output R3,
  output R2,
  output R1,
  output R0
);

  and and_1 (R7, B, A7);
  and and_2 (R6, B, A6);
  and and_3 (R5, B, A5);
  and and_4 (R4, B, A4);
  and and_5 (R3, B, A3);
  and and_6 (R2, B, A2);
  and and_7 (R1, B, A1);
  and and_8 (R0, B, A0);
endmodule
