// Logisim project cpu.circ as structural Verilog: 6 circuits, main circuit main
module main (
);

  wire AF, and_2_out, and_4_out, and_8_out, and_19_out, and_27_out, Auxiliary_ALU, BEF, BF, Carry_ALU,
       Carry_MUL_DIV, CLK, CLK0, CLK1, CLK2, CLK3, CLK4, CLK5, CLK6, CLK7, CLK8, CLK9, CLK10, CLK11, CLK12,
       CLK13, CLK14, CLK15, CMP, CMP_REG_IMM, CMP_REG_REG, CMP_TEST, DIV, ExecutionCondition, HALT,
       InstFetch, InstGroup0, InstGroup1, j_k_ff_1_qn, JMP, JMP_LABEL, JMP_REG, LEF, LegalInst, LegalSubInst,
       LegalSuperInst, LF, MATH, MATH_ALL_FLAGS_Unaffected, MATH_CF_Unaffected, MATH_REG_IMM, MATH_REG_REG,
       MOV_REG_IMM, MOV_REG_REG, MUL, MUL_DIV, multiplexer_7_out, multiplexer_10_out, multiplexer_23_out,
       NBEF, NBF, New_AF, New_CF, New_PF, New_SF, New_VF, New_ZF, NLEF, NLF, NOP, nor_1_out, not_2_out, NSF,
       NVF, NZF, or_1_out, or_2_out, or_3_out, or_4_out, or_5_out, or_8_out, or_9_out, or_15_out, or_16_out,
       Overflow_ALU, Parity_ALU, PF, R_ALU_SH_BIT, RESET, SF, Sign_ALU, SubInst0, SubInst1, SubInst2,
       SubInst3, SubInst4, SubInst5, SubInst6, SubInst7, SubInst8, SubInst9, SubInst10, SubInst11, SubInst12,
       SubInst13, SubInst14, SubInst15, SubInstGroup0, SubInstGroup1, TEST, TEST_REG_IMM, TEST_REG_REG,
       Update_ALL_FLAGS, Update_CF, VF, Zero_ALU, ZF;
  wire [0:0] multiplexer_11_out_2;
  wire [2:0] priority_encoder_1_out;
  wire [3:0] MATH_ALU_OP, multiplexer_8_out;
  wire [5:1] FLAGS_q, undriven;
  wire [6:0] multiplexer_12_out;
  wire [7:0] A_ALU, AL, BL, CL, CLK_COUNTER, CurrentInst, CurrentInstArg1, CurrentInstArg2, CurrentSubInst,
       DL, JMP_PC, multiplexer_4_out, multiplexer_5_out, multiplexer_11_out, multiplexer_16_out,
       multiplexer_17_out, not_3_out, PC, R_ALU, REGRLine, RH_ALU_R, RL_ALU_R;
  wire [7:7] multiplexer_6_out;
  wire [15:0] multiplexer_1_out;
  wire [31:0] ram_1_dout;
  wire [39:0] MATH_ALUWLine, MUL_DIV_ALUWLine;
  wire [39:8] ALUWLine;
  wire [43:0] HALT_MainWLine, NOP_MainWLine;
  wire [44:0] MainWLine, MATH_MainWLine, MOV_REG_IMM_MainWLine, MOV_REG_REG_MainWLine, MUL_DIV_MainWLine;

  Multiplexer multiplexer_1 (.in0(1'b1), .in1(ZF), .out(multiplexer_1_out[0]), .sel(CurrentInst[3]));
  Multiplexer multiplexer_2 (.in0(PF), .in1(AF), .out(multiplexer_1_out[14]), .sel(CurrentInst[3]));
  or or_1 (or_1_out, ~ExecutionCondition, MainWLine[44]);  // OR_Gate
  and and_1 (LegalSuperInst, ~CurrentInst[1], ~CurrentInst[2]);  // AND_Gate
  not not_1 (multiplexer_1_out[15], multiplexer_1_out[14]);
  Counter CLockCounter (
    .clr(RESET), .load(or_2_out), .up(1'b1), .clk(CLK), .D({8{1'b0}}), .Q(CLK_COUNTER));  // open: count, carry
  and and_2 (and_2_out, or_1_out, j_k_ff_1_qn);
  Decoder decoder_1 (.out0(InstGroup0), .out1(InstGroup1), .sel(CurrentInst[0]), .en(LegalInst));
  Multiplexer #(.enable("true"), .select(4)) multiplexer_3 (
    .in0(multiplexer_1_out[0]), .in1(NZF), .in2(SF), .in3(NSF), .in4(NLEF), .in5(NLF), .in6(LF), .in7(LEF),
    .in8(NBEF), .in9(NBF), .in10(BF), .in11(BEF), .in12(VF), .in13(NVF), .in14(multiplexer_1_out[14]),
    .in15(multiplexer_1_out[15]), .out(ExecutionCondition), .sel(CurrentInst[7:4]), .en(LegalSuperInst));
  or or_2 (or_2_out, and_2_out, InstFetch);
  // Probe on A_ALU
  and and_3 (LegalInst, j_k_ff_1_qn, LegalSuperInst, LegalSubInst);
  // Probe on ALUWLine[15:8]
  Counter InstructionPointer (
    .clr(RESET), .load(JMP), .up(1'b1), .count(and_2_out), .clk(CLK), .D(JMP_PC), .Q(PC));  // open: carry
  J_K_Flip_Flop j_k_ff_1 (
    .J(or_3_out), .K(and_4_out), .clk(or_4_out), .Q(InstFetch), .Qn(j_k_ff_1_qn));  // open: preset, reset
  or or_3 (or_3_out, and_2_out, RESET);
  and and_4 (and_4_out, ~RESET, InstFetch);  // AND_Gate
  or or_4 (or_4_out, RESET, CLK);
  Decoder #(.enable("false"), .select(4)) decoder_2 (
    .out0(CLK0), .out1(CLK1), .out2(CLK2), .out3(CLK3), .out4(CLK4), .out5(CLK5), .out6(CLK6), .out7(CLK7),
    .out8(CLK8), .out9(CLK9), .out10(CLK10), .out11(CLK11), .out12(CLK12), .out13(CLK13), .out14(CLK14),
    .out15(CLK15), .sel(CLK_COUNTER[3:0]));
  Decoder #(.select(4)) decoder_3 (
    .out0(SubInst0), .out1(SubInst1), .out2(SubInst2), .out3(SubInst3), .out4(SubInst4), .out5(SubInst5),
    .out6(SubInst6), .out7(SubInst7), .out8(SubInst8), .out9(SubInst9), .out10(SubInst10), .out11(SubInst11),
    .out12(SubInst12), .out13(SubInst13), .out14(SubInst14), .out15(SubInst15), .sel(CurrentSubInst[3:0]),
    .en(LegalInst));
  Multiplexer #(.width(8)) multiplexer_4 (.in0(MainWLine[31:24]), .in1(PC), .out(multiplexer_4_out), .sel(InstFetch));
  and and_5 (LegalSubInst, ~CurrentSubInst[5], ~CurrentSubInst[6], ~CurrentSubInst[7]);  // AND_Gate
  // Probe on R_ALU
  ByteALU bytealu_1 (
    .A(A_ALU), .B(ALUWLine[15:8]), .Op(ALUWLine[35:32]), .R(R_ALU), .Carry(Carry_ALU),
    .AuxiliaryCarry(Auxiliary_ALU), .Zero(Zero_ALU), .Negative(Sign_ALU), .EvenParity(Parity_ALU),
    .Overflow(Overflow_ALU));
  not not_2 (not_2_out, CurrentSubInst[4]);
  RAM #(.dataWidth(32), .enables("line")) ram_1 (
    .addr(multiplexer_4_out), .we(MainWLine[43]), .clk(CLK), .dout(ram_1_dout));  // open: din
  and and_6 (SubInstGroup0, not_2_out, LegalSubInst);
  and and_7 (SubInstGroup1, CurrentSubInst[4], LegalSubInst);
  // Probe on RL_ALU_R
  // Probe on ALUWLine[23:16]
  // Probe on RH_ALU_R
  // Probe on ALUWLine[31:24]
  Register #(.width(32)) register_1 (
    .D(ram_1_dout), .en(InstFetch), .clk(CLK),
    .Q({CurrentInst, CurrentSubInst, CurrentInstArg1, CurrentInstArg2}), .clr(RESET));
  // Probe on {multiplexer_5_out[0], not_3_out[7:1]}
  Multiplexer #(.width(8)) multiplexer_5 (
    .in0(RL_ALU_R), .in1(ALUWLine[23:16]), .out({multiplexer_5_out[0], not_3_out[7:1]}), .sel(ALUWLine[36]));
  Multiplexer #(.width(8)) multiplexer_6 (
    .in0(RH_ALU_R), .in1(ALUWLine[31:24]), .out({multiplexer_6_out[7], multiplexer_5_out[7:1]}),
    .sel(ALUWLine[36]));
  // Probe on {multiplexer_6_out[7], multiplexer_5_out[7:1]}
  not not_3 (not_3_out[0], Sign_ALU);
  MUL_DIV_REG_INST mul_div_reg_inst_1 (
    .MUL_EN(MUL), .DIV_EN(DIV), .CLK0(CLK0), .CLK1(CLK1), .CLK2(CLK2), .CLK3(CLK3), .CLK4(CLK4), .CLK5(CLK5),
    .CLK6(CLK6), .CLK7(CLK7), .CLK8(CLK8), .CLK9(CLK9), .CLK10(CLK10), .CLK11(CLK11),
    .REG_ARG1(CurrentInstArg1), .REG_ARG2(CurrentInstArg2), .REGR_Line(REGRLine), .R_ALU(R_ALU),
    .RL_ALU(RL_ALU_R), .RH_ALU(RH_ALU_R), .Sign_ALU(Sign_ALU), .R_ALU_SH_BIT(R_ALU_SH_BIT),
    .MainWLine(MUL_DIV_MainWLine), .ALUWLine(MUL_DIV_ALUWLine), .Carry(Carry_MUL_DIV));
  MATH_REG_ARG_INST math_reg_arg_inst_1 (
    .EN(MATH), .CLK0(CLK0), .CLK1(CLK1), .ImmArg2(MATH_REG_IMM), .CMP_TEST(CMP_TEST), .ALU_OP(MATH_ALU_OP),
    .REG_ARG1(CurrentInstArg1), .Inst_ARG2(CurrentInstArg2), .REGR_Line(REGRLine), .R_ALU(R_ALU),
    .RL_ALU(RL_ALU_R), .MainWLine(MATH_MainWLine), .ALUWLine(MATH_ALUWLine));
  MOV_REG_IMM_INST mov_reg_imm_inst_1 (
    .EN(MOV_REG_IMM), .CLK0(CLK0), .REG_ARG(CurrentInstArg1), .IMM_ARG(CurrentInstArg2),
    .MainWLine(MOV_REG_IMM_MainWLine));
  MOV_REG_REG_INST mov_reg_reg_inst_1 (
    .EN(MOV_REG_REG), .CLK0(CLK0), .REG_S_ARG(CurrentInstArg1), .REG_D_ARG(CurrentInstArg2),
    .REGR_Line(REGRLine), .MainWLine(MOV_REG_REG_MainWLine));
  Clock clock_1 (.out(CLK));
  Button button_1 (.out(RESET));
  Multiplexer multiplexer_7 (
    .in0(multiplexer_6_out[7]), .in1(multiplexer_11_out_2[0]), .out(multiplexer_7_out), .sel(ALUWLine[39]));
  LED FETCH (.in(InstFetch));
  nor nor_1 (nor_1_out, InstFetch, HALT);
  LED EXECUTE (.in(nor_1_out));
  LED u_HALT (.in(HALT));
  // Probe on AL
  Registers registers_1 (
    .EnableWrite(MainWLine[41]), .EnableRead(MainWLine[40]), .Write(MainWLine[23:16]),
    .REGWSelect(MainWLine[15:8]), .REGRSelect(MainWLine[7:0]), .CLK(CLK), .RESET(RESET), .Read(REGRLine),
    .AL(AL), .BL(BL), .CL(CL), .DL(DL));
  // Probe on CL
  Multiplexer #(.width(4)) multiplexer_8 (.in0(4'b0111), .in1(4'b0000), .out(multiplexer_8_out), .sel(TEST));
  // Probe on BL
  // Probe on DL
  Multiplexer #(.width(4)) multiplexer_9 (
    .in0(CurrentSubInst[3:0]), .in1(multiplexer_8_out), .out(MATH_ALU_OP), .sel(CMP_TEST));
  Multiplexer multiplexer_10 (.in0(R_ALU_SH_BIT), .in1(multiplexer_7_out), .out(multiplexer_10_out), .sel(or_5_out));
  or or_5 (or_5_out, ALUWLine[37], ALUWLine[39]);
  // Probe on {multiplexer_5_out[0], not_3_out[7:1]}
  Multiplexer #(.width(8)) multiplexer_11 (
    .in0({multiplexer_5_out[0], not_3_out[7:1]}), .in1(not_3_out),
    .out({multiplexer_11_out[6:0], multiplexer_11_out_2[0]}), .sel(ALUWLine[37]));
  // Probe on not_3_out
  // Probe on {multiplexer_6_out[7], multiplexer_5_out[7:1]}
  Multiplexer #(.width(8)) multiplexer_12 (
    .in0({multiplexer_6_out[7], multiplexer_5_out[7:1]}), .in1(multiplexer_5_out),
    .out({multiplexer_12_out, multiplexer_11_out[7]}), .sel(ALUWLine[37]));
  // Probe on multiplexer_5_out
  D_Flip_Flop d_ff_1 (.D(multiplexer_10_out), .clk(CLK), .Q(R_ALU_SH_BIT), .reset(RESET));  // open: Qn, preset
  // Probe on {multiplexer_11_out[6:0], multiplexer_11_out_2[0]}
  // Probe on {multiplexer_12_out, multiplexer_11_out[7]}
  LED CF (.in(BF));
  LED u_PF (.in(PF));
  LED u_VF (.in(VF));
  LED u_AF (.in(AF));
  LED u_ZF (.in(ZF));
  LED u_SF (.in(SF));
  Multiplexer #(.width(40)) multiplexer_13 (
    .in0(MUL_DIV_ALUWLine), .in1(MATH_ALUWLine), .out({ALUWLine, A_ALU}), .sel(MATH));
  Multiplexer #(.width(8)) multiplexer_14 (.in0(CurrentInstArg1), .in1(REGRLine), .out(JMP_PC), .sel(JMP_REG));
  assign NOP_MainWLine[7:0] = JMP_REG ? CurrentInstArg1 : 8'bz;  // Controlled_Buffer controlled_buffer_1
  Hex_Digit_Display #(.decimalPoint("false")) hex_digit_display_1 (.value(AL[7:4]));
  Hex_Digit_Display #(.decimalPoint("false")) hex_digit_display_2 (.value(PC[7:4]));
  Hex_Digit_Display #(.decimalPoint("false")) hex_digit_display_3 (.value(CurrentInst[7:4]));
  and and_8 (and_8_out, InstGroup0, SubInstGroup0, ExecutionCondition);
  Hex_Digit_Display #(.decimalPoint("false")) hex_digit_display_4 (.value(AL[3:0]));
  Hex_Digit_Display #(.decimalPoint("false")) hex_digit_display_5 (.value(BL[7:4]));
  Hex_Digit_Display #(.decimalPoint("false")) hex_digit_display_6 (.value(PC[3:0]));
  Hex_Digit_Display #(.decimalPoint("false")) hex_digit_display_7 (.value(CLK_COUNTER[7:4]));
  Hex_Digit_Display #(.decimalPoint("false")) hex_digit_display_8 (.value(CurrentInst[3:0]));
  Hex_Digit_Display #(.decimalPoint("false")) hex_digit_display_9 (.value(CurrentSubInst[7:4]));
  Hex_Digit_Display #(.decimalPoint("false")) hex_digit_display_10 (.value(BL[3:0]));
  Hex_Digit_Display #(.decimalPoint("false")) hex_digit_display_11 (.value(CLK_COUNTER[3:0]));
  Hex_Digit_Display #(.decimalPoint("false")) hex_digit_display_12 (.value(CurrentSubInst[3:0]));
  Priority_Encoder priority_encoder_1 (
    .in0(NOP), .in1(HALT), .in2(JMP), .in3(MOV_REG_IMM), .in4(MOV_REG_REG), .in5(MUL), .in6(DIV), .in7(MATH),
    .out(priority_encoder_1_out));  // open: en_in, gs, en_out
  // Probe on {multiplexer_11_out[6:0], multiplexer_11_out_2[0]}
  // Probe on multiplexer_11_out
  // Probe on {multiplexer_12_out, multiplexer_11_out[7]}
  // Probe on {Carry_ALU, multiplexer_12_out}
  Hex_Digit_Display #(.decimalPoint("false")) hex_digit_display_13 (.value(CL[7:4]));
  Hex_Digit_Display #(.decimalPoint("false")) hex_digit_display_14 (.value(CL[3:0]));
  Hex_Digit_Display #(.decimalPoint("false")) hex_digit_display_15 (.value(RH_ALU_R[7:4]));
  Hex_Digit_Display #(.decimalPoint("false")) hex_digit_display_16 (.value(RH_ALU_R[3:0]));
  Hex_Digit_Display #(.decimalPoint("false")) hex_digit_display_17 (.value(CurrentInstArg1[7:4]));
  Hex_Digit_Display #(.decimalPoint("false")) hex_digit_display_18 (.value(CurrentInstArg1[3:0]));
  and and_9 (NOP, and_8_out, SubInst0);
  and and_10 (HALT, and_8_out, SubInst1);
  and and_11 (JMP_LABEL, and_8_out, SubInst2);
  and and_12 (JMP_REG, and_8_out, SubInst3);
  and and_13 (MOV_REG_IMM, and_8_out, SubInst4);
  and and_14 (MOV_REG_REG, and_8_out, SubInst5);
  and and_15 (MUL, and_8_out, SubInst6);
  and and_16 (DIV, and_8_out, SubInst7);
  Multiplexer #(.select(3), .width(45)) multiplexer_15 (
    .in0({1'b1, NOP_MainWLine}), .in1({1'b0, HALT_MainWLine}), .in2({1'b1, NOP_MainWLine}),
    .in3(MOV_REG_IMM_MainWLine), .in4(MOV_REG_REG_MainWLine), .in5(MUL_DIV_MainWLine),
    .in6(MUL_DIV_MainWLine), .in7(MATH_MainWLine), .out(MainWLine), .sel(priority_encoder_1_out));
  Multiplexer #(.width(8)) multiplexer_16 (
    .in0({multiplexer_11_out[6:0], multiplexer_11_out_2[0]}), .in1(multiplexer_11_out),
    .out(multiplexer_16_out), .sel(ALUWLine[39]));
  Multiplexer #(.width(8)) multiplexer_17 (
    .in0({multiplexer_12_out, multiplexer_11_out[7]}), .in1({Carry_ALU, multiplexer_12_out}),
    .out(multiplexer_17_out), .sel(ALUWLine[39]));
  Hex_Digit_Display #(.decimalPoint("false")) hex_digit_display_19 (.value(DL[7:4]));
  Hex_Digit_Display #(.decimalPoint("false")) hex_digit_display_20 (.value(DL[3:0]));
  Hex_Digit_Display #(.decimalPoint("false")) hex_digit_display_21 (.value(RL_ALU_R[7:4]));
  Hex_Digit_Display #(.decimalPoint("false")) hex_digit_display_22 (.value(RL_ALU_R[3:0]));
  Hex_Digit_Display #(.decimalPoint("false")) hex_digit_display_23 (.value(CurrentInstArg2[7:4]));
  Hex_Digit_Display #(.decimalPoint("false")) hex_digit_display_24 (.value(CurrentInstArg2[3:0]));
  or or_6 (JMP, JMP_LABEL, JMP_REG);
  or or_7 (MUL_DIV, MUL, DIV);
  or or_8 (or_8_out, ALUWLine[39], ALUWLine[36]);
  or or_9 (or_9_out, ALUWLine[37], ALUWLine[38]);
  // Probe on multiplexer_16_out
  // Probe on multiplexer_17_out
  // Shift_Register #(.length(16)) shift_register_1: pin names not known; wires that end beside it: RESET, or_8_out, or_9_out, CLK, ALUWLine[38]
  and and_17 (MATH, InstGroup1, ExecutionCondition);
  // Probe on RL_ALU_R
  // Probe on RH_ALU_R
  Multiplexer multiplexer_18 (.in0(PF), .in1(Parity_ALU), .out(New_PF), .sel(Update_ALL_FLAGS));
  Multiplexer multiplexer_19 (.in0(VF), .in1(Overflow_ALU), .out(New_VF), .sel(Update_ALL_FLAGS));
  Multiplexer multiplexer_20 (.in0(AF), .in1(Auxiliary_ALU), .out(New_AF), .sel(Update_ALL_FLAGS));
  Multiplexer multiplexer_21 (.in0(ZF), .in1(Zero_ALU), .out(New_ZF), .sel(Update_ALL_FLAGS));
  Multiplexer multiplexer_22 (.in0(SF), .in1(Sign_ALU), .out(New_SF), .sel(Update_ALL_FLAGS));
  Register FLAGS (
    .D({New_SF, New_ZF, undriven[5], New_AF, New_VF, New_PF, undriven[1], New_CF}), .en(1'b1), .clk(CLK),
    .Q({SF, ZF, FLAGS_q[5], AF, VF, PF, FLAGS_q[1], BF}), .clr(RESET));
  Multiplexer multiplexer_23 (.in0(Carry_ALU), .in1(Carry_MUL_DIV), .out(multiplexer_23_out), .sel(MUL_DIV));
  and and_18 (MATH_REG_REG, MATH, SubInstGroup0);
  and and_19 (and_19_out, MATH, SubInstGroup1);
  and and_20 (CMP_REG_IMM, MATH_REG_REG, SubInst8);
  and and_21 (CMP_REG_REG, MATH_REG_REG, SubInst9);
  and and_22 (TEST_REG_IMM, MATH_REG_REG, SubInst10);
  and and_23 (TEST_REG_REG, MATH_REG_REG, SubInst11);
  Multiplexer multiplexer_24 (.in0(BF), .in1(multiplexer_23_out), .out(New_CF), .sel(Update_CF));
  not not_4 (NBF, BF);
  not not_5 (NVF, VF);
  not not_6 (NZF, ZF);
  not not_7 (NSF, SF);
  xor xor_1 (LF, SF, VF);
  or or_10 (LEF, LF, ZF);
  or or_11 (BEF, BF, ZF);
  not not_8 (NLEF, LEF);
  not not_9 (NLF, LF);
  not not_10 (NBEF, BEF);
  or or_12 (CMP, CMP_REG_IMM, CMP_REG_REG);
  or or_13 (TEST, TEST_REG_IMM, TEST_REG_REG);
  or or_14 (MATH_REG_IMM, and_19_out, CMP_REG_IMM, TEST_REG_IMM);
  or or_15 (or_15_out, SubInst8, SubInst15);
  or or_16 (or_16_out, SubInst10, SubInst11);
  or or_17 (CMP_TEST, CMP, TEST);
  and and_24 (MATH_ALL_FLAGS_Unaffected, and_19_out, or_15_out);
  and and_25 (MATH_CF_Unaffected, and_19_out, or_16_out);
  and and_26 (Update_ALL_FLAGS, MATH, ~MATH_ALL_FLAGS_Unaffected);  // AND_Gate
  and and_27 (and_27_out, Update_ALL_FLAGS, ~MATH_CF_Unaffected);  // AND_Gate
  or or_18 (Update_CF, and_27_out, MUL_DIV);

  // Other names for the same wires on the sheet: CF = BF; ALUWLine[7:0] = A_ALU; B_ALU[7:0] = ALUWLine[15:8];
  //   RL_ALU_W[7:0] = ALUWLine[23:16]; RH_ALU_W[7:0] = ALUWLine[31:24]; OP_ALU[3:0] = ALUWLine[35:32];
  //   LOAD_R_ALU = ALUWLine[36]; SHL_R_ALU = ALUWLine[37]; SHL_SET_R_ALU = ALUWLine[38]; SHR_R_ALU = ALUWLine[39];
  //   Instruction_REG[31:0] = {CurrentInst, CurrentSubInst, CurrentInstArg1, CurrentInstArg2};
  //   ExtraConditionalInst = CurrentInst[3]; REGRSelect[7:0] = MainWLine[7:0]; REGWSelect[7:0] = MainWLine[15:8];
  //   REGWLine[7:0] = MainWLine[23:16]; MEMSelect[7:0] = MainWLine[31:24]; MEMWLine[7:0] = MainWLine[39:32];
  //   REGR = MainWLine[40]; REGW = MainWLine[41]; MEMR = MainWLine[42]; MEMW = MainWLine[43]

  // Notes on the sheet:
  //   Const. 1 means the instruction is executed unconditionally
  //   ExStateLine
  //   R_ALUStateLine
  //   HALT
  //   NOP
  //   In reality, VF is on bit #11
  //   NOT_REG
  //   MIRROR_REG
  //   INC_REG
  //   DEC_REG
endmodule

module Registers (
  input  EnableWrite,
  input  EnableRead,
  input  [7:0] Write,
  input  [7:0] REGWSelect,
  input  [7:0] REGRSelect,
  input  CLK,
  input  RESET,
  output [7:0] Read,
  output [7:0] AL,
  output [7:0] BL,
  output [7:0] CL,
  output [7:0] DL
);

  wire demultiplexer_1_out0, demultiplexer_1_out1, demultiplexer_1_out2, demultiplexer_1_out3;
  wire [7:0] demultiplexer_2_out0, demultiplexer_2_out1, demultiplexer_2_out2, demultiplexer_2_out3;

  Demultiplexer #(.select(2)) demultiplexer_1 (
    .out0(demultiplexer_1_out0), .out1(demultiplexer_1_out1), .out2(demultiplexer_1_out2),
    .out3(demultiplexer_1_out3), .in(EnableWrite), .sel(REGWSelect[1:0]));
  Demultiplexer #(.select(2), .width(8)) demultiplexer_2 (
    .out0(demultiplexer_2_out0), .out1(demultiplexer_2_out1), .out2(demultiplexer_2_out2),
    .out3(demultiplexer_2_out3), .in(Write), .sel(REGWSelect[1:0]));
  Register AL_REG (.D(demultiplexer_2_out0), .en(demultiplexer_1_out0), .clk(CLK), .Q(AL), .clr(RESET));
  Register BL_REG (.D(demultiplexer_2_out1), .en(demultiplexer_1_out1), .clk(CLK), .Q(BL), .clr(RESET));
  Register CL_REG (.D(demultiplexer_2_out2), .en(demultiplexer_1_out2), .clk(CLK), .Q(CL), .clr(RESET));
  Register DL_REG (.D(demultiplexer_2_out3), .en(demultiplexer_1_out3), .clk(CLK), .Q(DL), .clr(RESET));
  Multiplexer #(.enable("true"), .select(2), .width(8)) multiplexer_1 (
    .in0(AL), .in1(BL), .in2(CL), .in3(DL), .out(Read), .sel(REGRSelect[1:0]), .en(EnableRead));
endmodule

module MOV_REG_IMM_INST (
  input  EN,
  input  CLK0,
  input  [7:0] REG_ARG,
  input  [7:0] IMM_ARG,
  output [44:0] MainWLine
);

  and and_1 (MainWLine[44], EN, CLK0);

  assign {MainWLine[43:40], MainWLine[23:8]} = {2'b00, MainWLine[44], 1'b0, IMM_ARG, REG_ARG};
endmodule

module MOV_REG_REG_INST (
  input  EN,
  input  CLK0,
  input  [7:0] REG_S_ARG,
  input  [7:0] REG_D_ARG,
  input  [7:0] REGR_Line,
  output [44:0] MainWLine
);

  and and_1 (MainWLine[44], EN, CLK0);

  assign {MainWLine[43:40], MainWLine[23:0]} = {2'b00, {2{MainWLine[44]}}, REGR_Line, REG_S_ARG, REG_D_ARG};
endmodule

module MUL_DIV_REG_INST (
  input  MUL_EN,
  input  DIV_EN,
  input  CLK0,
  input  CLK1,
  input  CLK2,
  input  CLK3,
  input  CLK4,
  input  CLK5,
  input  CLK6,
  input  CLK7,
  input  CLK8,
  input  CLK9,
  input  CLK10,
  input  CLK11,
  input  [7:0] REG_ARG1,
  input  [7:0] REG_ARG2,
  input  [7:0] REGR_Line,
  input  [7:0] R_ALU,
  input  [7:0] RL_ALU,
  input  [7:0] RH_ALU,
  input  Sign_ALU,
  input  R_ALU_SH_BIT,
  output [44:0] MainWLine,
  output [39:0] ALUWLine,
  output Carry
);

  wire CLK0_t, CLK9_t, CLK10_t, CLK11_t, EN, FINAL_CLKS, FINAL_END_CLKS, LOOPED_CLKS, multiplexer_1_out,
       not_1_out, or_2_out;
  wire [7:0] multiplexer_4_out;
  wire [36:24] LOOPED_ALUWLine;
  wire [39:0] INIT_FINAL_ALUWLine;
  wire [39:8] INIT_FINAL_MainWLine, LOOPED_MainWLine;

  and and_1 (CLK0_t, EN, CLK0);
  not not_1 (not_1_out, Sign_ALU);
  or or_1 (EN, MUL_EN, DIV_EN);
  or or_2 (or_2_out, CLK1, CLK2, CLK3, CLK4, CLK5, CLK6, CLK7, CLK8);
  not not_2 (INIT_FINAL_ALUWLine[36], FINAL_END_CLKS);
  and and_2 (LOOPED_CLKS, EN, or_2_out);
  Multiplexer multiplexer_1 (.in0(R_ALU_SH_BIT), .in1(not_1_out), .out(multiplexer_1_out), .sel(DIV_EN));
  Multiplexer #(.width(8)) multiplexer_2 (
    .in0(RH_ALU), .in1(R_ALU), .out(LOOPED_ALUWLine[31:24]), .sel(multiplexer_1_out));
  and and_3 (INIT_FINAL_ALUWLine[39], INIT_FINAL_ALUWLine[36], MUL_EN);
  and and_4 (LOOPED_ALUWLine[36], INIT_FINAL_ALUWLine[36], multiplexer_1_out);
  Multiplexer #(.width(8)) multiplexer_3 (
    .in0(REG_ARG1), .in1(REG_ARG2), .out(INIT_FINAL_MainWLine[15:8]), .sel(CLK10_t));
  and and_5 (INIT_FINAL_ALUWLine[37], INIT_FINAL_ALUWLine[36], DIV_EN);
  and and_6 (CLK9_t, EN, CLK9);
  and and_7 (CLK10_t, EN, CLK10);
  and and_8 (CLK11_t, EN, CLK11);
  Multiplexer #(.width(8)) multiplexer_4 (
    .in0(RH_ALU), .in1({R_ALU_SH_BIT, RH_ALU[7:1]}), .out(multiplexer_4_out), .sel(DIV_EN));
  or or_3 (Carry, multiplexer_4_out[4], multiplexer_4_out[7], multiplexer_4_out[6], multiplexer_4_out[5], multiplexer_4_out[3], multiplexer_4_out[2], multiplexer_4_out[1], multiplexer_4_out[0]);
  or or_4 (FINAL_CLKS, CLK9_t, CLK10_t);
  or or_5 (FINAL_END_CLKS, CLK11_t, FINAL_CLKS);
  Multiplexer #(.width(45)) multiplexer_5 (
    .in0({CLK11_t, 2'b00, FINAL_CLKS, 1'b1, INIT_FINAL_MainWLine, REG_ARG1}),
    .in1({3'b000, FINAL_CLKS, 1'b1, LOOPED_MainWLine, REG_ARG2}), .out(MainWLine), .sel(LOOPED_CLKS));
  Multiplexer #(.width(40)) multiplexer_6 (
    .in0({INIT_FINAL_ALUWLine[39], 1'b0, INIT_FINAL_ALUWLine[37:32], {8{1'b0}}, REGR_Line, INIT_FINAL_ALUWLine[15:0]}),
    .in1({INIT_FINAL_ALUWLine[39], 1'b0, INIT_FINAL_ALUWLine[37], LOOPED_ALUWLine[36], 3'b011, DIV_EN, LOOPED_ALUWLine[31:24], RL_ALU, REGR_Line, RH_ALU}),
    .out(ALUWLine), .sel(LOOPED_CLKS));
  Multiplexer #(.width(8)) multiplexer_7 (
    .in0(RL_ALU), .in1(multiplexer_4_out), .out(INIT_FINAL_MainWLine[23:16]), .sel(CLK10_t));

  // Other names for the same wires on the sheet: INIT_FINAL_MainWLine (some bits) = {CLK11_t, FINAL_CLKS, REG_ARG1};
  //   REGRSelect_INIT[7:0] = REG_ARG1; REGWSelect_FINAL[7:0] = INIT_FINAL_MainWLine[15:8];
  //   REGWLine_FINAL[7:0] = INIT_FINAL_MainWLine[23:16];
  //   LOOPED_ALUWLine (some bits) = {INIT_FINAL_ALUWLine[39], INIT_FINAL_ALUWLine[37], DIV_EN, RL_ALU, REGR_Line, RH_ALU};
  //   INIT_FINAL_ALUWLine[23:16] = REGR_Line; RH_ALU_LOOPED[7:0] = LOOPED_ALUWLine[31:24]; DIV = DIV_EN;
  //   OP_ALU_LOOPED[0] = DIV_EN; LOOPED_MainWLine (some bits) = {FINAL_CLKS, REG_ARG2};
  //   REGRSelect_LOOPED[7:0] = REG_ARG2; IO_State[1] = FINAL_CLKS; REGW = FINAL_CLKS; MUL = MUL_EN

  // Notes on the sheet:
  //   or if DIV, load if the subtraction result is not negative
  //   Write results only on final clocks
  //   Select first REG to read to init RL with it
  //   Select second REG to read to send it to B_ALU
  //   Only load R_ALU to RH_ALU if the shifted bit of MUL is set,
  //   MEMSelect
  //   MEMWLine
  //   REGWSelect
  //   REGWLine
  //   MEMSelect
  //   MEMWLine
  //   CLK10 writes to second REG, otherwise first REG
  //   LOAD_R_ALU
  //   SHL_R_ALU
  //   SHL_SET_R_ALU
  //   SHR_R_ALU
  //   LOAD_R_ALU
  //   SHL_R_ALU
  //   SHL_SET_R_ALU
  //   SHR_R_ALU
  //   if MUL, op is ADD (0b0110), if DIV op is SUB (0b0111)
  //   Init RL with first REG (with shift) and zeroize RH
  //   Always load RH to A_ALU, REG_ARG to B_ALU, and RL will be shifted only
  //   RL_ALU_W
  //   RH_ALU_W
  //   R_ALUStateLine
  //   RL_ALU_W
  //   RH_ALU_W
  //   R_ALUStateLine
  //   A_ALU
  //   B_ALU
  //   OP_ALU
  //   A_ALU
  //   B_ALU
  //   OP_ALU
  //   CLK9 writes RL to first REG
  //    but RL must be shifted in that CLK
  //   This shifted bit is shifted back after division
  //   as RH shouldn't be shifted in final looped CLK
  //   CLK10 writes RH to second REG if op is MUL, if DIV, shifts RH to right
endmodule

module MATH_REG_ARG_INST (
  input  EN,
  input  CLK0,
  input  CLK1,
  input  ImmArg2,
  input  CMP_TEST,
  input  [3:0] ALU_OP,
  input  [7:0] REG_ARG1,
  input  [7:0] Inst_ARG2,
  input  [7:0] REGR_Line,
  input  [7:0] R_ALU,
  input  [7:0] RL_ALU,
  output [44:0] MainWLine,
  output [39:0] ALUWLine
);

  wire and_3_out, CLK1_t;

  and and_1 (ALUWLine[36], EN, CLK0);
  and and_2 (CLK1_t, EN, CLK1);
  and and_3 (and_3_out, ALUWLine[36], ImmArg2);
  and and_4 (MainWLine[41], ~CMP_TEST, MainWLine[44]);  // AND_Gate
  or or_1 (MainWLine[44], CLK1_t, and_3_out);
  Multiplexer #(.width(8)) multiplexer_1 (.in0(REGR_Line), .in1(Inst_ARG2), .out(ALUWLine[15:8]), .sel(ImmArg2));
  Multiplexer #(.width(8)) multiplexer_2 (.in0(REG_ARG1), .in1(Inst_ARG2), .out(MainWLine[7:0]), .sel(CLK1_t));
  Multiplexer #(.width(8)) multiplexer_3 (.in0(RL_ALU), .in1(REGR_Line), .out(ALUWLine[7:0]), .sel(ImmArg2));

  assign {ALUWLine[39:37], ALUWLine[35:32], ALUWLine[23:16]} = {3'b000, ALU_OP, REGR_Line};
  assign {MainWLine[43:42], MainWLine[40], MainWLine[23:8]} = {3'b001, R_ALU, REG_ARG1};

  // Other names for the same wires on the sheet: Op[3:0] = ALU_OP; CLK0_t = ALUWLine[36]; ARG2[7:0] = Inst_ARG2;
  //   REGW = MainWLine[41]; SecondArgIsImm = ImmArg2

  // Notes on the sheet:
  //   SHL_SET_R_ALU
  //   LOAD_R_ALU
  //   SHL_R_ALU
  //   SHR_R_ALU
  //   If second arg is imm, write to REG1 and set the fetch signal after one clock cycle
  //   REGRSelect
  //   REGWSelect
  //   MEMSelect
  //   InstFetch_State
  //   R_ALUStateLine
  //   REGWLine
  //   MEMWLine
  //   IO_State
  //   A_ALU
  //   B_ALU
  //   RL_ALU_W
  //   RH_ALU_W
  //   OP_ALU
endmodule
